# Fritzing sketch M6E_EthernetShield (saved by Fritzing 0.9.3b)
breadboards: 1

parts:
  Internet_Facing_Uno = Arduino Ethernet Shield (Rev3)
  SparkFun_Simultaneous_RFID_Reader_-_M6E_Nano1 = SparkFun Simultaneous RFID Reader - M6E Nano [part_number=SEN-14066]
  U1 = LIPO-1000mAh [package=lipo-1000]
  U2 = LIPO-1000mAh [package=lipo-1000]
  R1 = Resistor [tolerance=±5% resistance=220 package=THT]
  LED1 = smd LED [color="Green (555nm)" package="0603 [SMD]"]
  LED2 = smd LED [color="Red (633nm)" package="0603 [SMD]"]
  R2 = Resistor [tolerance=±5% resistance=220 package=THT]
  R3 = Resistor [tolerance=±5% resistance=220 package=THT]

nets:
  N1: Internet_Facing_Uno.D8, SparkFun_Simultaneous_RFID_Reader_-_M6E_Nano1.ENABLE, R1.Pin_0
  N2: Internet_Facing_Uno.D2, SparkFun_Simultaneous_RFID_Reader_-_M6E_Nano1.SOFT-RX
  N3: Internet_Facing_Uno.PWM_D3, SparkFun_Simultaneous_RFID_Reader_-_M6E_Nano1.SOFT-TX
  N4: Internet_Facing_Uno.PWM_D6, R3.Pin_1
  GND: Internet_Facing_Uno.GND, SparkFun_Simultaneous_RFID_Reader_-_M6E_Nano1.GND, U1.-, U2.-, R1.Pin_1, LED1.cathode, LED2.cathode
  N5: SparkFun_Simultaneous_RFID_Reader_-_M6E_Nano1.N$12, U1.+, U2.+
  N6: LED1.anode, R2.Pin_0
  N7: LED2.anode, R3.Pin_0

custom parts:
  SparkFun Simultaneous RFID Reader - M6E Nano: Description: The SparkFun Simultaneous RFID Reader is an Arduino-compatible board to get you started with the M6E Nano UHF RFID Reader. Radio Frequency Identification (RFID) is becoming popular everywhere for tracking practically everything. Whether you want to get started by adding an RFID reader on your toolbox with tags on all your tools or allowing access to the tree house for your secret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
